# Fritzing sketch TambourineLight (saved by Fritzing 0.9.3b)
circuit board: 5.6cm x 2cm
perfboards: 1

parts:
  U1 = attiny85 [package=dip]
  J1 = screw terminal, 4 pins
  S1 = Pushbutton [package="[THT]"]
  R1 = Resistor [tolerance=±5% resistance=10k package=THT]
  LED1 = Super Flux RGB LED (com. anode)
  R2 = Resistor [tolerance=±5% resistance=47 package=THT]
  LED2 = RGB LED - (4 legs) [package="5 mm [THT]"]

nets:
  N1: U1.Pin_2, J1.pin4, R1.Pin_1
  N2: U1.Pin_3, LED1.blue_cathode, LED2.blue_cathode
  N3: U1.Pin_4, J1.pin2, J1.pin3, S1.Pin_3, S1.Pin_4, R1.Pin_0
  N4: U1.Pin_5, R2.Pin_0
  N5: U1.Pin_6, LED1.green_cathode, LED2.green_cathode
  N6: U1.Pin_7, S1.Pin_1, S1.Pin_2
  N7: U1.Pin_8, J1.pin1, LED1.common_anode, LED2.common_anode
  N8: LED1.red_cathode, R2.Pin_1, LED2.red_cathode

notes:
  bjjDrumLight 1.0
  + - - s
